# Fritzing sketch cds_led (saved by Fritzing 0.8.7b)
breadboards: 1

parts:
  부품1 = Arduino Uno (Rev3)
  R1 = Resistor [tolerance=±5% resistance=10k package=THT]
  R2 = Photocell (LDR) [package=THT]
  LED2 = LED - 5mm [color="Red (633nm)" package="5 mm [THT]"]
  R3 = Resistor [tolerance=±5% resistance=330 package=THT]

nets:
  N1: 부품1.A0, R1.Pin_1, R2.pin_1
  N2: 부품1.D12/MISO, LED2.anode
  N3: 부품1.5V, R2.pin_0
  N4: 부품1.GND, R1.Pin_0, R3.Pin_0
  N5: LED2.cathode, R3.Pin_1
